# Fritzing sketch IoT-Modified-Action-Man-Figure-with-Laser-Beams (saved by Fritzing 0.9.3b)
breadboards: 3

parts:
  U1 = NodeMCU V3.0
  Part1 = KY-008 Laser Transmitter Module [package="Breakout board"]
  Part2 = KY-008 Laser Transmitter Module [package="Breakout board"]
  LED1 = RGB LED (com. anode, rbg) [package="5 mm [THT]"]

nets:
  N1: U1.D0, Part2.S
  N2: U1.D1, Part1.S
  N3: U1.D2, LED1.red_cathode
  N4: U1.D3, LED1.common_anode
  N5: U1.D4, LED1.green_cathode
  N6: U1.3V3, LED1.blue_cathode
  N7: U1.GND#6, U1.GND#13, U1.GND#16, U1.GND#33
  N8: U1.GND#41, Part1.-, Part2.-

custom parts:
  NodeMCU V3.0: ESP8266 based NodeMCU
  KY-008 Laser Transmitter Module: Laser Transmitter module KY-008 for Arduino, emits a dot shaped red laser beam.
